// Logisim project xor_example_pla.circ as structural Verilog: 1 circuit, main circuit main
module main (
  input  X,
  input  Y,
  output Z
);

  wire and_1_out, and_2_out, not_1_out, not_2_out;

  not not_1 (not_1_out, Y);
  not not_2 (not_2_out, X);
  and and_1 (and_1_out, not_2_out, Y);
  and and_2 (and_2_out, X, not_1_out);
  or or_1 (Z, and_2_out, and_1_out);
endmodule
