// Logisim project xor_subcircuit.circ as structural Verilog: 2 circuits, main circuit main
module main (
  input  X,
  input  Y,
  output X_XOR_Y
);

  \xor  xor_1 (.X(X), .Y(Y), .X_XOR_Y(X_XOR_Y));
endmodule

module \xor  (
  input  X,
  input  Y,
  output X_XOR_Y
);

  wire and_1_out, and_2_out, not_1_out, not_2_out;

  not not_1 (not_1_out, Y);
  not not_2 (not_2_out, X);
  and and_1 (and_1_out, not_2_out, Y);
  and and_2 (and_2_out, X, not_1_out);
  or or_1 (X_XOR_Y, and_2_out, and_1_out);
endmodule
