// Logisim project e2522225.circ as structural Verilog: 1 circuit, main circuit main
module main (
  input  O0,
  input  A1,
  input  A0,
  input  B1,
  input  B0,
  input  O1,
  input  O2,
  input  O3,
  output Z,
  output L0,
  output L1,
  output L2,
  output L3,
  output L4,
  output L5,
  output L6,
  output L7,
  output L8,
  output L9,
  output S,
  output C,
  output P,
  output L,
  output E,
  output G
);

  wire and_1_out, and_2_out, and_3_out, and_4_out, and_5_out, and_6_out, and_7_out, and_8_out, and_9_out,
       and_10_out, and_11_out, and_12_out, and_13_out, and_14_out, and_15_out, and_16_out, and_17_out,
       and_18_out, and_19_out, and_20_out, and_21_out, and_22_out, and_23_out, and_24_out, and_25_out,
       and_26_out, and_27_out, and_28_out, and_29_out, and_30_out, and_31_out, and_32_out, and_33_out,
       and_34_out, and_35_out, and_36_out, and_37_out, and_38_out, and_39_out, and_40_out, and_41_out,
       n3_to_8_decoder_74138_1_p7, n3_to_8_decoder_74138_1_p8, n3_to_8_decoder_74138_1_p9,
       n3_to_8_decoder_74138_1_p10, n3_to_8_decoder_74138_1_p11, n3_to_8_decoder_74138_1_p12,
       n3_to_8_decoder_74138_1_p13, n3_to_8_decoder_74138_1_p14, n3_to_8_decoder_74138_2_p7,
       n3_to_8_decoder_74138_2_p8, n3_to_8_decoder_74138_2_p9, n3_to_8_decoder_74138_3_p2,
       n3_to_8_decoder_74138_3_p3, n3_to_8_decoder_74138_3_p7, n3_to_8_decoder_74138_3_p8,
       n3_to_8_decoder_74138_3_p9, n3_to_8_decoder_74138_3_p10, n3_to_8_decoder_74138_3_p11,
       n3_to_8_decoder_74138_3_p12, n3_to_8_decoder_74138_4_p7, n3_to_8_decoder_74138_4_p8,
       n3_to_8_decoder_74138_4_p9, n3_to_8_decoder_74138_4_p10, n3_to_8_decoder_74138_5_p7,
       n3_to_8_decoder_74138_5_p8, n3_to_8_decoder_74138_5_p9, n3_to_8_decoder_74138_5_p10,
       n3_to_8_decoder_74138_5_p11, n3_to_8_decoder_74138_5_p12, n3_to_8_decoder_74138_5_p13,
       n3_to_8_decoder_74138_6_p7, n3_to_8_decoder_74138_6_p8, n3_to_8_decoder_74138_6_p9,
       n3_to_8_decoder_74138_6_p10, n3_to_8_decoder_74138_7_p7, n3_to_8_decoder_74138_7_p8,
       n3_to_8_decoder_74138_7_p9, n3_to_8_decoder_74138_7_p10, n3_to_8_decoder_74138_8_p7,
       n3_to_8_decoder_74138_8_p8, n3_to_8_decoder_74138_8_p9, n3_to_8_decoder_74138_8_p10,
       n3_to_8_decoder_74138_9_p7, n3_to_8_decoder_74138_9_p8, n3_to_8_decoder_74138_9_p9,
       n3_to_8_decoder_74138_9_p10, nor_1_out, not_1_out, not_2_out, not_3_out, not_4_out, not_5_out,
       not_6_out, not_7_out, not_8_out, not_9_out, not_10_out, not_11_out, not_12_out, not_13_out,
       not_14_out, not_15_out, not_16_out, not_17_out, not_18_out, not_19_out, not_20_out, not_21_out,
       not_22_out, not_23_out, not_24_out, not_25_out, not_26_out, not_27_out, not_28_out, not_29_out,
       not_30_out, not_32_out, not_33_out, not_34_out, not_35_out, not_36_out, not_37_out, not_38_out,
       not_39_out, not_40_out, not_41_out, not_42_out, not_43_out, not_44_out, not_45_out, not_46_out,
       not_47_out, not_48_out, or_1_out, or_2_out, or_3_out, or_4_out, or_5_out, or_6_out, or_7_out,
       or_8_out, or_9_out, or_10_out, or_11_out, or_12_out, or_13_out, or_14_out, or_15_out, or_16_out,
       or_17_out, or_18_out, or_19_out, or_20_out, or_21_out, or_22_out, or_23_out, or_24_out, or_25_out,
       or_26_out, or_27_out, or_28_out, or_29_out, or_30_out, or_31_out, or_32_out, or_33_out, or_34_out,
       or_35_out, or_42_out, or_43_out, xnor_1_out, xnor_2_out, xor_1_out, xor_2_out, xor_3_out, xor_4_out,
       xor_5_out, xor_6_out, xor_7_out;

  // _3_to_8_decoder__74138 #(.Facing("east")) 3_to_8_decoder_74138_1: pin names not known; wires that end beside it: O0, O1, O2, 1'b1, 1'b0, 1'b0, n3_to_8_decoder_74138_1_p7, n3_to_8_decoder_74138_1_p8, n3_to_8_decoder_74138_1_p9, n3_to_8_decoder_74138_1_p10, n3_to_8_decoder_74138_1_p11, n3_to_8_decoder_74138_1_p12, n3_to_8_decoder_74138_1_p13, n3_to_8_decoder_74138_1_p14
  not not_1 (not_1_out, n3_to_8_decoder_74138_1_p7);
  not not_2 (not_2_out, n3_to_8_decoder_74138_1_p8);
  not not_3 (not_3_out, n3_to_8_decoder_74138_1_p9);
  not not_4 (not_4_out, n3_to_8_decoder_74138_1_p10);
  not not_5 (not_5_out, n3_to_8_decoder_74138_1_p11);
  not not_6 (not_6_out, n3_to_8_decoder_74138_1_p12);
  not not_7 (not_7_out, n3_to_8_decoder_74138_1_p13);
  not not_8 (not_8_out, n3_to_8_decoder_74138_1_p14);
  not not_9 (not_9_out, A1);
  not not_10 (not_10_out, A0);
  not not_11 (not_11_out, B1);
  not not_12 (not_12_out, B0);
  and and_1 (and_1_out, A0, not_12_out);
  and and_2 (and_2_out, A0, B1);
  and and_3 (and_3_out, B1, B0);
  and and_4 (and_4_out, A0, B0);
  and and_5 (and_5_out, A0, B1);
  and and_6 (and_6_out, A1, B1);
  and and_7 (and_7_out, A1, B0);
  or or_1 (or_1_out, A0, not_12_out);
  and and_8 (and_8_out, A1, not_11_out);
  and and_9 (and_9_out, A0, not_11_out);
  and and_10 (and_10_out, A0, B0);
  and and_11 (and_11_out, B1, A1);
  xor xor_1 (xor_1_out, A0, B0);
  and and_12 (and_12_out, A1, not_10_out);
  and and_13 (and_13_out, B1, not_12_out);
  and and_14 (and_14_out, not_9_out, B1);
  and and_15 (and_15_out, not_9_out, not_10_out);
  and and_16 (and_16_out, and_15_out, B0);
  and and_17 (and_17_out, not_10_out, and_18_out);
  and and_18 (and_18_out, B1, B0);
  and and_19 (and_19_out, not_9_out, not_10_out);
  and and_20 (and_20_out, and_19_out, B0);
  and and_21 (and_21_out, not_9_out, B1);
  and and_22 (and_22_out, not_10_out, B1);
  and and_23 (and_23_out, and_22_out, B0);
  xnor xnor_1 (xnor_1_out, A1, B1);
  xnor xnor_2 (xnor_2_out, A0, B0);
  and and_24 (and_24_out, A0, not_11_out);
  and and_25 (and_25_out, and_24_out, not_12_out);
  and and_26 (and_26_out, A1, A0);
  and and_27 (and_27_out, and_26_out, not_12_out);
  and and_28 (and_28_out, A1, not_11_out);
  and and_29 (and_29_out, A1, B1);
  and and_30 (and_30_out, A0, B0);
  xor xor_2 (xor_2_out, B0, A0);
  xor xor_3 (xor_3_out, A1, B1);
  or or_2 (or_2_out, A0, B0);
  or or_3 (or_3_out, A1, B1);
  and and_31 (and_31_out, not_9_out, and_2_out);
  and and_32 (and_32_out, and_3_out, not_10_out);
  and and_33 (and_33_out, and_5_out, and_7_out);
  and and_34 (and_34_out, A1, or_1_out);
  xor xor_4 (xor_4_out, A0, B0);
  xor xor_5 (xor_5_out, A1, B1);
  xor xor_6 (xor_6_out, A1, B1);
  and and_35 (and_35_out, and_12_out, B0);
  and and_36 (and_36_out, A0, and_13_out);
  or or_4 (or_4_out, and_16_out, and_17_out);
  or or_5 (or_5_out, and_21_out, and_23_out);
  and and_37 (and_37_out, xnor_1_out, xnor_2_out);
  or or_6 (or_6_out, and_27_out, and_28_out);
  or or_7 (or_7_out, and_1_out, and_31_out);
  and and_38 (and_38_out, and_32_out, A1);
  and and_39 (and_39_out, and_33_out, and_6_out);
  or or_8 (or_8_out, and_34_out, and_9_out);
  xor xor_7 (xor_7_out, and_10_out, xor_5_out);
  and and_40 (and_40_out, and_10_out, xor_5_out);
  or or_9 (or_9_out, and_40_out, and_11_out);
  and and_41 (and_41_out, xor_6_out, nor_1_out);
  nor nor_1 (nor_1_out, and_35_out, and_36_out);
  or or_10 (or_10_out, and_14_out, or_4_out);
  or or_11 (or_11_out, and_20_out, or_5_out);
  and and_42 (L, or_11_out, not_6_out);
  and and_43 (E, and_37_out, not_6_out);
  or or_12 (or_12_out, and_25_out, or_6_out);
  and and_44 (G, or_12_out, not_6_out);
  // _3_to_8_decoder__74138 #(.Facing("east")) 3_to_8_decoder_74138_2: pin names not known; wires that end beside it: or_7_out, and_38_out, 1'b0, not_1_out, 1'b0, 1'b0, n3_to_8_decoder_74138_2_p7, n3_to_8_decoder_74138_2_p8, n3_to_8_decoder_74138_2_p9
  // _3_to_8_decoder__74138 #(.Facing("east")) 3_to_8_decoder_74138_3: pin names not known; wires that end beside it: and_4_out, n3_to_8_decoder_74138_3_p2, n3_to_8_decoder_74138_3_p3, not_2_out, L9, L9, n3_to_8_decoder_74138_3_p7, n3_to_8_decoder_74138_3_p8, n3_to_8_decoder_74138_3_p9, n3_to_8_decoder_74138_3_p10, n3_to_8_decoder_74138_3_p11, n3_to_8_decoder_74138_3_p12
  xor xor_8 (n3_to_8_decoder_74138_3_p2, and_5_out, and_7_out);
  xor xor_9 (n3_to_8_decoder_74138_3_p3, and_6_out, and_33_out);
  and and_45 (L9, and_39_out, not_2_out);
  // _3_to_8_decoder__74138 #(.Facing("east")) 3_to_8_decoder_74138_4: pin names not known; wires that end beside it: or_8_out, and_8_out, 1'b0, not_3_out, 1'b0, 1'b0, n3_to_8_decoder_74138_4_p7, n3_to_8_decoder_74138_4_p8, n3_to_8_decoder_74138_4_p9, n3_to_8_decoder_74138_4_p10
  // _3_to_8_decoder__74138 #(.Facing("east")) 3_to_8_decoder_74138_5: pin names not known; wires that end beside it: xor_4_out, xor_7_out, or_9_out, not_4_out, 1'b0, 1'b0, n3_to_8_decoder_74138_5_p7, n3_to_8_decoder_74138_5_p8, n3_to_8_decoder_74138_5_p9, n3_to_8_decoder_74138_5_p10, n3_to_8_decoder_74138_5_p11, n3_to_8_decoder_74138_5_p12, n3_to_8_decoder_74138_5_p13
  // _3_to_8_decoder__74138 #(.Facing("east")) 3_to_8_decoder_74138_6: pin names not known; wires that end beside it: xor_1_out, and_41_out, 1'b0, not_5_out, 1'b0, 1'b0, n3_to_8_decoder_74138_6_p7, n3_to_8_decoder_74138_6_p8, n3_to_8_decoder_74138_6_p9, n3_to_8_decoder_74138_6_p10
  // _3_to_8_decoder__74138 #(.Facing("east")) 3_to_8_decoder_74138_7: pin names not known; wires that end beside it: and_30_out, and_29_out, 1'b0, not_7_out, 1'b0, 1'b0, n3_to_8_decoder_74138_7_p7, n3_to_8_decoder_74138_7_p8, n3_to_8_decoder_74138_7_p9, n3_to_8_decoder_74138_7_p10
  // _3_to_8_decoder__74138 #(.Facing("east")) 3_to_8_decoder_74138_8: pin names not known; wires that end beside it: xor_2_out, xor_3_out, 1'b0, not_8_out, 1'b0, 1'b0, n3_to_8_decoder_74138_8_p7, n3_to_8_decoder_74138_8_p8, n3_to_8_decoder_74138_8_p9, n3_to_8_decoder_74138_8_p10
  // _3_to_8_decoder__74138 #(.Facing("east")) 3_to_8_decoder_74138_9: pin names not known; wires that end beside it: or_2_out, or_3_out, 1'b0, O3, 1'b0, 1'b0, n3_to_8_decoder_74138_9_p7, n3_to_8_decoder_74138_9_p8, n3_to_8_decoder_74138_9_p9, n3_to_8_decoder_74138_9_p10
  not not_13 (not_13_out, n3_to_8_decoder_74138_2_p7);
  not not_14 (not_14_out, n3_to_8_decoder_74138_2_p8);
  not not_15 (not_15_out, n3_to_8_decoder_74138_2_p9);
  not not_16 (not_16_out, n3_to_8_decoder_74138_3_p7);
  not not_17 (not_17_out, n3_to_8_decoder_74138_3_p8);
  not not_18 (not_18_out, n3_to_8_decoder_74138_3_p9);
  not not_19 (not_19_out, n3_to_8_decoder_74138_3_p10);
  not not_20 (not_20_out, n3_to_8_decoder_74138_3_p11);
  not not_21 (not_21_out, n3_to_8_decoder_74138_3_p12);
  not not_22 (not_22_out, n3_to_8_decoder_74138_4_p7);
  not not_23 (not_23_out, n3_to_8_decoder_74138_4_p8);
  not not_24 (not_24_out, n3_to_8_decoder_74138_4_p9);
  not not_25 (not_25_out, n3_to_8_decoder_74138_4_p10);
  and and_46 (C, not_4_out, or_9_out);
  and and_47 (S, not_5_out, or_10_out);
  not not_26 (not_26_out, n3_to_8_decoder_74138_5_p7);
  not not_27 (not_27_out, n3_to_8_decoder_74138_5_p8);
  not not_28 (not_28_out, n3_to_8_decoder_74138_5_p9);
  not not_29 (not_29_out, n3_to_8_decoder_74138_5_p10);
  not not_30 (not_30_out, n3_to_8_decoder_74138_5_p11);
  not not_31 (L5, n3_to_8_decoder_74138_5_p12);
  not not_32 (not_32_out, n3_to_8_decoder_74138_5_p13);
  not not_33 (not_33_out, n3_to_8_decoder_74138_6_p7);
  not not_34 (not_34_out, n3_to_8_decoder_74138_6_p8);
  not not_35 (not_35_out, n3_to_8_decoder_74138_6_p9);
  not not_36 (not_36_out, n3_to_8_decoder_74138_6_p10);
  not not_37 (not_37_out, n3_to_8_decoder_74138_7_p7);
  not not_38 (not_38_out, n3_to_8_decoder_74138_7_p8);
  not not_39 (not_39_out, n3_to_8_decoder_74138_7_p9);
  not not_40 (not_40_out, n3_to_8_decoder_74138_7_p10);
  not not_41 (not_41_out, n3_to_8_decoder_74138_8_p7);
  not not_42 (not_42_out, n3_to_8_decoder_74138_8_p8);
  not not_43 (not_43_out, n3_to_8_decoder_74138_8_p9);
  not not_44 (not_44_out, n3_to_8_decoder_74138_8_p10);
  not not_45 (not_45_out, n3_to_8_decoder_74138_9_p7);
  not not_46 (not_46_out, n3_to_8_decoder_74138_9_p8);
  not not_47 (not_47_out, n3_to_8_decoder_74138_9_p9);
  not not_48 (not_48_out, n3_to_8_decoder_74138_9_p10);
  or or_13 (or_13_out, not_13_out, not_16_out);
  or or_14 (or_14_out, not_22_out, not_26_out);
  or or_15 (or_15_out, not_33_out, not_37_out);
  or or_16 (or_16_out, not_41_out, not_45_out);
  or or_17 (or_17_out, not_14_out, not_17_out);
  or or_18 (or_18_out, not_23_out, not_27_out);
  or or_19 (or_19_out, not_34_out, not_38_out);
  or or_20 (or_20_out, not_42_out, not_46_out);
  or or_21 (or_21_out, not_15_out, not_18_out);
  or or_22 (or_22_out, not_24_out, not_28_out);
  or or_23 (or_23_out, not_35_out, not_39_out);
  or or_24 (or_24_out, not_43_out, not_47_out);
  or or_25 (or_25_out, not_19_out, not_25_out);
  or or_26 (or_26_out, not_29_out, not_36_out);
  or or_27 (or_27_out, not_40_out, not_44_out);
  or or_28 (or_28_out, or_13_out, or_14_out);
  or or_29 (or_29_out, or_15_out, or_16_out);
  or or_30 (or_30_out, or_17_out, or_18_out);
  or or_31 (or_31_out, or_19_out, or_20_out);
  or or_32 (or_32_out, or_21_out, or_22_out);
  or or_33 (or_33_out, or_23_out, or_24_out);
  or or_34 (or_34_out, or_25_out, or_26_out);
  or or_35 (or_35_out, or_27_out, not_48_out);
  or or_36 (L4, not_20_out, not_30_out);
  or or_37 (L6, not_21_out, not_32_out);
  or or_38 (L0, or_28_out, or_29_out);
  or or_39 (L1, or_30_out, or_31_out);
  or or_40 (L2, or_32_out, or_33_out);
  or or_41 (L3, or_34_out, or_35_out);
  or or_42 (or_42_out, L3, L1);
  or or_43 (or_43_out, L5, or_42_out);
  or or_44 (P, L9, or_43_out);

  assign L7 = 1'b0;
  assign L8 = 1'b0;
  assign Z = L0;
endmodule
